// Logisim project alu.circ as structural Verilog: 2 circuits, main circuit alu
module alu (
  input  [31:0] A,
  input  [31:0] B,
  input  [3:0] ALUSel,
  output [31:0] Result
);

  wire comparator_1_lt;
  wire [4:0] Bshift;
  wire [31:0] add0, and0, mul0, mulh0, mulhu0, negator_1_out, or0, sll0, slt0, sra0, srl0, sub0, xor0;

  Bit_Extender #(.in_width(32), .out_width(5), .\type ("zero")) bit_extender_1 (.in(B), .out(Bshift));
  Negator #(.width(32)) negator_1 (.in(B), .out(negator_1_out));
  Adder #(.width(32)) adder_1 (.a(A), .b(B), .out(add0));  // open: cin, cout
  assign and0 = A & B;  // AND_Gate and_1, 32 bits wide
  assign or0 = A | B;  // OR_Gate or_1, 32 bits wide
  assign xor0 = A ^ B;  // XOR_Gate xor_1, 32 bits wide
  Shifter #(.shift("lr"), .width(32)) shifter_1 (.in(A), .\dist (Bshift), .out(srl0));
  Shifter #(.shift("ar"), .width(32)) shifter_2 (.in(A), .\dist (Bshift), .out(sra0));
  Shifter #(.width(32)) shifter_3 (.in(A), .\dist (Bshift), .out(sll0));
  Comparator #(.width(32)) comparator_1 (.a(A), .b(B), .lt(comparator_1_lt));  // open: gt, eq
  Multiplier #(.width(32)) multiplier_1 (.a(A), .b(B), .out(mul0), .cout(mulhu0));  // open: cin
  Multiplier #(.mode("twosComplement"), .width(32)) multiplier_2 (.a(A), .b(B), .cout(mulh0));  // open: out, cin
  Adder #(.width(32)) adder_2 (.a(A), .b(negator_1_out), .out(sub0));  // open: cin, cout
  assign slt0 = {{31{1'b0}}, comparator_1_lt};  // Bit_Extender bit_extender_2
  Multiplexer #(.enable("false"), .select(4), .width(32)) multiplexer_1 (
    .in0(add0), .in1(and0), .in2(or0), .in3(xor0), .in4(srl0), .in5(sra0), .in6(sll0), .in7(slt0),
    .in10(mul0), .in11(mulhu0), .in12(sub0), .in13(B), .in14(mulh0), .out(Result), .sel(ALUSel));  // open: in8, in9, in15

  // Notes on the sheet:
  //   INPUTS to your circuit
  //   DON'T CHANGE THE LOCATIONS OF THE INPUTS AND OUTPUTS!
  //   OUTPUT from your circuit
endmodule

module sll1 (
  input  [31:0] A,
  input  [31:0] B,
  output [31:0] result
);

  wire [30:0] bit_extender_1_out;

  Bit_Extender #(.in_width(32), .out_width(31), .\type ("zero")) bit_extender_1 (.in(A), .out(bit_extender_1_out));
  Multiplexer #(.enable("false"), .width(32)) multiplexer_1 (
    .in0({bit_extender_1_out, 1'b0}), .in1(A));  // open: out, sel

  // Notes on the sheet:
  //   Incomplete use built-in shifter
endmodule
