// Logisim project control_logic.circ as structural Verilog: 1 circuit, main circuit control_logic
module control_logic (
  input  [31:0] inst,
  input  BrEq,
  input  BrLt,
  output PCSel,
  output RegWEn,
  output [2:0] ImmSel,
  output BrUn,
  output ASel,
  output BSel,
  output [3:0] ALUSel,
  output MemRW,
  output [1:0] WBSel,
  output CSRSel,
  output CSRWen,
  output [1:0] MemSel
);

  wire and_2_out, and_3_out, and_4_out, bitselector_1_out, comparator_10_eq, comparator_11_eq, isAUIPC,
       isBranch, isI, isJAL, isJALR, isLoad, isLUI, isMul, isR, multiplexer_1_out, not_1_out, not_2_out,
       not_3_out, not_4_out, not_5_out, or_5_out, or_8_out;
  wire [1:0] multiplexer_13_out;
  wire [2:0] multiplexer_2_out, multiplexer_3_out, multiplexer_4_out, multiplexer_5_out;
  wire [3:0] multiplexer_6_out, multiplexer_7_out, multiplexer_8_out, multiplexer_9_out, multiplexer_10_out,
       multiplexer_11_out;

  BitSelector #(.width(32)) bitselector_1 (.in(inst), .out(bitselector_1_out), .sel(5'b11001));
  and and_1 (isMul, bitselector_1_out, isR);
  Comparator #(.mode("unsigned"), .width(5)) comparator_1 (.a(inst[6:2]), .b(5'b01100), .eq(isR));  // open: gt, lt
  Comparator #(.mode("unsigned"), .width(5)) comparator_2 (.a(inst[6:2]), .b(5'b00100), .eq(isI));  // open: gt, lt
  Comparator #(.mode("unsigned"), .width(5)) comparator_3 (.a(inst[6:2]), .b({5{1'b0}}), .eq(isLoad));  // open: gt, lt
  Comparator #(.mode("unsigned"), .width(5)) comparator_4 (.a(inst[6:2]), .b(5'b01000), .eq(MemRW));  // open: gt, lt
  Comparator #(.mode("unsigned"), .width(5)) comparator_5 (.a(inst[6:2]), .b(5'b11000), .eq(isBranch));  // open: gt, lt
  Comparator #(.mode("unsigned"), .width(5)) comparator_6 (.a(inst[6:2]), .b(5'b11011), .eq(isJAL));  // open: gt, lt
  Comparator #(.mode("unsigned"), .width(5)) comparator_7 (.a(inst[6:2]), .b(5'b11001), .eq(isJALR));  // open: gt, lt
  Comparator #(.mode("unsigned"), .width(5)) comparator_8 (.a(inst[6:2]), .b(5'b01101), .eq(isLUI));  // open: gt, lt
  Comparator #(.mode("unsigned"), .width(5)) comparator_9 (.a(inst[6:2]), .b(5'b00101), .eq(isAUIPC));  // open: gt, lt
  not not_1 (not_1_out, BrEq);
  not not_2 (not_2_out, BrLt);
  Multiplexer #(.enable("false"), .select(3)) multiplexer_1 (
    .in0(BrEq), .in1(not_1_out), .in4(BrLt), .in5(not_2_out), .in6(BrLt), .in7(not_2_out),
    .out(multiplexer_1_out), .sel(inst[14:12]));  // open: in2, in3
  or or_1 (ASel, isBranch, isJAL, isAUIPC);
  and and_2 (and_2_out, isBranch, multiplexer_1_out);
  or or_2 (PCSel, isJAL, and_2_out, isJALR);
  or or_3 (BSel, isLUI, isI, MemRW, isLoad, isJALR, isJAL, isAUIPC, isBranch);
  or or_4 (RegWEn, isR, isI, isLoad, isJAL, isJALR, isLUI, isAUIPC);
  not not_3 (not_3_out, isI);
  and and_3 (and_3_out, not_3_out, inst[30]);
  Multiplexer #(.enable("false"), .width(3)) multiplexer_2 (
    .in0(3'b000), .in1(3'b001), .out(multiplexer_2_out), .sel(MemRW));
  Multiplexer #(.enable("false"), .width(3)) multiplexer_3 (
    .in0(3'b000), .in1(3'b010), .out(multiplexer_3_out), .sel(isBranch));
  Multiplexer #(.enable("false"), .width(3)) multiplexer_4 (
    .in0(3'b000), .in1(3'b100), .out(multiplexer_4_out), .sel(isJAL));
  Multiplexer #(.enable("false"), .width(3)) multiplexer_5 (
    .in0(3'b000), .in1(3'b011), .out(multiplexer_5_out), .sel(or_5_out));
  or or_5 (or_5_out, isLUI, isAUIPC);
  Multiplexer #(.enable("false"), .width(4)) multiplexer_6 (
    .in0(4'b0000), .in1(4'b1100), .out(multiplexer_6_out), .sel(and_3_out));
  Multiplexer #(.enable("false"), .width(4)) multiplexer_7 (
    .in0(4'b0100), .in1(4'b0101), .out(multiplexer_7_out), .sel(inst[30]));
  assign ImmSel = multiplexer_2_out | multiplexer_3_out | multiplexer_4_out | multiplexer_5_out;  // OR_Gate or_6, 3 bits wide
  Multiplexer #(.enable("false"), .select(3), .width(4)) multiplexer_8 (
    .in0(multiplexer_6_out), .in1(4'b0110), .in2(4'b0111), .in4(4'b0011), .in5(multiplexer_7_out),
    .in6(4'b0010), .in7(4'b0001), .out(multiplexer_8_out), .sel(inst[14:12]));  // open: in3
  Multiplexer #(.enable("false"), .select(2), .width(4)) multiplexer_9 (
    .in0(4'b1010), .in1(4'b1110), .in3(4'b1011), .out(multiplexer_9_out), .sel(inst[13:12]));  // open: in2
  Multiplexer #(.enable("false"), .width(4)) multiplexer_10 (
    .in0(multiplexer_8_out), .in1(multiplexer_9_out), .out(multiplexer_10_out), .sel(isMul));
  Multiplexer #(.enable("false"), .width(4)) multiplexer_11 (
    .in0(multiplexer_10_out), .in1(4'b1101), .out(multiplexer_11_out), .sel(isLUI));
  Multiplexer #(.enable("false"), .width(4)) multiplexer_12 (
    .in0(multiplexer_11_out), .in1(4'b0000), .out(ALUSel), .sel(and_4_out));
  and and_4 (and_4_out, not_4_out, not_5_out);
  not not_4 (not_4_out, isI);
  not not_5 (not_5_out, isR);
  Comparator #(.mode("unsigned"), .width(3)) comparator_10 (
    .a(3'b110), .b(inst[14:12]), .eq(comparator_10_eq));  // open: gt, lt
  Comparator #(.mode("unsigned"), .width(3)) comparator_11 (
    .a(3'b111), .b(inst[14:12]), .eq(comparator_11_eq));  // open: gt, lt
  or or_7 (BrUn, comparator_10_eq, comparator_11_eq);
  Multiplexer #(.enable("false"), .width(2)) multiplexer_13 (
    .in0(2'b01), .in1(2'b00), .out(multiplexer_13_out), .sel(isLoad));
  Multiplexer #(.enable("false"), .width(2)) multiplexer_14 (
    .in0(multiplexer_13_out), .in1(2'b10), .out(WBSel), .sel(or_8_out));
  or or_8 (or_8_out, isJAL, isJALR);

  assign CSRSel = inst[14];
  assign CSRWen = 1'b1;
  assign MemSel = inst[13:12];

  // Other names for the same wires on the sheet: inst2_6[4:0] = inst[6:2]; inst12_14[2:0] = inst[14:12];
  //   isStore = MemRW

  // Notes on the sheet:
  //   INPUTS to your circuit
  //   DON'T CHANGE THE LOCATIONS OF THE INPUTS AND OUTPUTS!
  //   OUTPUT from your circuit
endmodule
