// Logisim project control_logic_rom.circ as structural Verilog: 1 circuit, main circuit control_logic
module control_logic (
  input  [31:0] inst,
  input  BrEq,
  input  BrLt,
  output PCSel,
  output RegWEn,
  output [2:0] ImmSel,
  output BrUn,
  output ASel,
  output BSel,
  output [3:0] ALUSel,
  output MemRW,
  output [1:0] WBSel,
  output CSRSel,
  output CSRWen
);

  ROM #(.addrWidth(11), .dataWidth(17)) rom_1 (
    .addr({inst[6:2], inst[14:12], inst[30], BrEq, BrLt}),
    .data({PCSel, ImmSel, BrUn, ASel, BSel, ALUSel, MemRW, RegWEn, WBSel, CSRSel, CSRWen}));

  // Other names for the same wires on the sheet: inst12_14[2:0] = inst[14:12]; inst2_6[4:0] = inst[6:2]

  // Notes on the sheet:
  //   INPUTS to your circuit
  //   contents of rom_1 (hex, n*v repeats v):
  //   32*410 4*414 4*594 4*5d4 4*0 4*4d4 4*514 4*494 4*454 16*0 4*554 8*6614 12*2420 4*14 4*194 4*1d4 4*0
  //   4*d4 4*114 4*94 4*54 4*294 4*394 4*314 12*0 4*154 8*6374 4600 4600 4*14600 4600 4600 4600 14600 4600
  //   14600 14600 4600 14600 14600 5600 15600 5600 15600 15600 5600 15600 15600 4*10218 8*18618 8*0 4*15
  //   12*0 4*417
  //   DON'T CHANGE THE LOCATIONS OF THE INPUTS AND OUTPUTS!
  //   OUTPUT from your circuit
endmodule
