// Logisim project cpu.circ as structural Verilog: 1 circuit, main circuit cpu
module cpu (
  input  clk,
  input  [31:0] INSTRUCTION,
  input  [31:0] READ_DATA,
  output [31:0] WRITE_ADDRESS,
  output [31:0] PROGRAM_COUNTER,
  output [31:0] ra,
  output [31:0] sp,
  output [31:0] t0,
  output [31:0] t1,
  output [31:0] t2,
  output [31:0] s0,
  output [31:0] s1,
  output [31:0] a0,
  output [31:0] tohost,
  output [3:0] WRITE_ENABLE,
  output [31:0] WRITE_DATA
);

  wire ASel, BrEq, BrLt, BrUn, BSel, CSRSel, CSRWen, MemRW, PCSel, RegWEn;
  wire [1:0] MemSel, WBSel;
  wire [2:0] ImmSel;
  wire [3:0] ALUSel, bit_extender_8_out, MemMask, multiplexer_6_out, multiplexer_7_out;
  wire [11:0] CSRAddr;
  wire [19:0] inst_reg;
  wire [31:0] adder_1_out, adder_2_out, bit_extender_1_out, imm, MemByte0, MemByte1, MemByte2, MemByte3,
       MemHalfWord0, MemHalfWord1, MemRead, multiplexer_1_out, multiplexer_2_out, multiplexer_3_out,
       multiplexer_4_out, multiplexer_5_out, PC_reg, Read_Data_1, WB;

  Adder #(.width(32)) adder_1 (.a(PROGRAM_COUNTER), .b(32'h4), .out(adder_1_out));  // open: cin, cout
  Multiplexer #(.enable("false"), .width(32)) multiplexer_1 (
    .in0(adder_1_out), .in1(WRITE_ADDRESS), .out(multiplexer_1_out), .sel(PCSel));
  Register #(.width(32)) PC (.D(multiplexer_1_out), .en(1'b1), .clk(clk), .Q(PROGRAM_COUNTER));  // open: clr
  Register #(.width(32)) register_1 (
    .D(multiplexer_2_out), .en(1'b1), .clk(clk), .Q({CSRAddr, inst_reg}));  // open: clr
  Multiplexer #(.enable("false"), .width(32)) multiplexer_2 (
    .in0(INSTRUCTION), .in1(32'h13), .out(multiplexer_2_out), .sel(PCSel));
  Register #(.width(32)) register_2 (.D(PROGRAM_COUNTER), .en(1'b1), .clk(clk), .Q(PC_reg));  // open: clr
  control_logic control_logic_1 (
    .CSRWen(CSRWen), .MemSel(MemSel), .PCSel(PCSel), .RegWEn(RegWEn), .ImmSel(ImmSel), .BrUn(BrUn),
    .ASel(ASel), .BSel(BSel), .ALUSel(ALUSel), .MemRW(MemRW), .WBSel(WBSel), .CSRSel(CSRSel),
    .inst({CSRAddr, inst_reg}), .BrEq(BrEq), .BrLt(BrLt));
  imm_gen imm_gen_1 (.inst({CSRAddr, inst_reg}), .ImmSel(ImmSel), .imm(imm));
  regfile regfile_1 (
    .rs1(inst_reg[19:15]), .rs2(CSRAddr[4:0]), .rd(inst_reg[11:7]), .Write_Data(WB), .RegWEn(RegWEn),
    .clk(clk), .ra(ra), .sp(sp), .t0(t0), .t1(t1), .t2(t2), .s0(s0), .s1(s1), .a0(a0),
    .Read_Data_1(Read_Data_1), .Read_Data_2(WRITE_DATA));
  branch_comp branch_comp_1 (.rs1(Read_Data_1), .rs2(WRITE_DATA), .BrUn(BrUn), .BrEq(BrEq), .BrLt(BrLt));
  assign bit_extender_1_out = {{27{1'b0}}, inst_reg[19:15]};  // Bit_Extender bit_extender_1
  Multiplexer #(.enable("false"), .width(32)) multiplexer_3 (
    .in0(Read_Data_1), .in1(bit_extender_1_out), .out(multiplexer_3_out), .sel(CSRSel));
  Multiplexer #(.enable("false"), .width(32)) multiplexer_4 (
    .in0(Read_Data_1), .in1(PC_reg), .out(multiplexer_4_out), .sel(ASel));
  Multiplexer #(.enable("false"), .width(32)) multiplexer_5 (
    .in0(WRITE_DATA), .in1(imm), .out(multiplexer_5_out), .sel(BSel));
  alu alu_1 (.Result(WRITE_ADDRESS), .A(multiplexer_4_out), .B(multiplexer_5_out), .ALUSel(ALUSel));
  csr csr_1 (.CSR_address(CSRAddr), .CSR_din(multiplexer_3_out), .CSR_WE(CSRWen), .clk(clk), .tohost(tohost));
  Multiplexer #(.enable("false"), .select(2), .width(4)) multiplexer_6 (
    .in0(4'b0001), .in1(4'b0010), .in2(4'b0100), .in3(4'b1000), .out(multiplexer_6_out),
    .sel(WRITE_ADDRESS[1:0]));
  Multiplexer #(.enable("false"), .width(4)) multiplexer_7 (
    .in0(4'b0011), .in1(4'b1100), .out(multiplexer_7_out), .sel(WRITE_ADDRESS[1]));
  Multiplexer #(.enable("false"), .select(2), .width(4)) multiplexer_8 (
    .in0(multiplexer_6_out), .in1(multiplexer_7_out), .in2(4'b1111), .out(MemMask), .sel(MemSel));  // open: in3
  assign MemByte0 = {{24{READ_DATA[7]}}, READ_DATA[7:0]};  // Bit_Extender bit_extender_2
  assign MemByte1 = {{24{READ_DATA[15]}}, READ_DATA[15:8]};  // Bit_Extender bit_extender_3
  assign MemByte2 = {{24{READ_DATA[23]}}, READ_DATA[23:16]};  // Bit_Extender bit_extender_4
  assign MemByte3 = {{24{READ_DATA[31]}}, READ_DATA[31:24]};  // Bit_Extender bit_extender_5
  assign MemHalfWord0 = {{16{READ_DATA[15]}}, READ_DATA[15:0]};  // Bit_Extender bit_extender_6
  assign MemHalfWord1 = {{16{READ_DATA[31]}}, READ_DATA[31:16]};  // Bit_Extender bit_extender_7
  Multiplexer #(.enable("false"), .select(4), .width(32)) multiplexer_9 (
    .in1(MemByte0), .in2(MemByte1), .in3(MemHalfWord0), .in4(MemByte2), .in8(MemByte3), .in12(MemHalfWord1),
    .in15(READ_DATA), .out(MemRead), .sel(MemMask));  // open: in0, in5, in6, in7, in9, in10, in11, in13, in14
  assign bit_extender_8_out = {{3{MemRW}}, MemRW};  // Bit_Extender bit_extender_8
  assign WRITE_ENABLE = bit_extender_8_out & MemMask;  // AND_Gate and_1, 4 bits wide
  Adder #(.width(32)) adder_2 (.a(PC_reg), .b(32'h4), .out(adder_2_out));  // open: cin, cout
  Multiplexer #(.enable("false"), .select(2), .width(32)) multiplexer_10 (
    .in0(MemRead), .in1(WRITE_ADDRESS), .in2(adder_2_out), .out(WB), .sel(WBSel));  // open: in3

  // Other names for the same wires on the sheet: ALURes[31:0] = WRITE_ADDRESS; MemAdd_0_1[1:0] = WRITE_ADDRESS[1:0];
  //   MemAdd_1 = WRITE_ADDRESS[1]; rd[4:0] = inst_reg[11:7]; rs1[4:0] = inst_reg[19:15]; inst_reg[31:20] = CSRAddr;
  //   rs2[4:0] = CSRAddr[4:0]; Read_Data_2[31:0] = WRITE_DATA

  // Notes on the sheet:
  //   Output to IMEM
  //   IMEM (do **NOT** move this)
  //   Inputs from IMEM
  //   Inputs/Outputs for testing. Do **NOT** move these.
  //   Outputs To DMEM
  //   DMEM (do **NOT** move this)
  //   Inputs From DMEM
endmodule
